# Fritzing sketch watch_with_alarm_Encoder (saved by Fritzing 0.9.4)

parts:
  Компонент1 = Arduino Nano (Rev3.0) (ICSP)
  U2 = LCD-16X2 [package=lcd-16x2_noholes]
  LCM1602_IIC2 = LCM1602 IIC [part_number="LCM1602 IIC" chip_label="LCM1602 IIC" package="DIP (Dual Inline) [THT]"]
  PCB3 = RTC_DS1302_module
  J1 = Piezo Speaker  # not connected

nets:
  N1: Компонент1.D10, PCB3.RST
  N2: Компонент1.D11/MOSI, PCB3.DAT
  N3: Компонент1.D12/MISO, PCB3.CLK
  N4: Компонент1.A5, LCM1602_IIC2.SCL
  N5: Компонент1.A4, LCM1602_IIC2.SDA
  VSS: U2.VSS, LCM1602_IIC2.VSS
  VDD: U2.VDD, LCM1602_IIC2.VDD
  N6: U2.VO, LCM1602_IIC2.V0
  N7: U2.RS, LCM1602_IIC2.RS
  N8: U2.R_W, LCM1602_IIC2.RW
  N9: U2.E, LCM1602_IIC2.E
  N10: U2.DB0, LCM1602_IIC2.D0
  N11: U2.DB1, LCM1602_IIC2.D1
  N12: U2.DB2, LCM1602_IIC2.D2
  N13: U2.DB3, LCM1602_IIC2.D3
  N14: U2.DB4, LCM1602_IIC2.D4
  N15: U2.DB5, LCM1602_IIC2.D5
  N16: U2.DB6, LCM1602_IIC2.D6
  N17: U2.DB7, LCM1602_IIC2.D7
  N18: U2.A, LCM1602_IIC2.A
  N19: U2.K, LCM1602_IIC2.K

custom parts:
  LCM1602 IIC: I2C-Module to use a 1602 or 2004 LCD on with the wire.h libory Serial LCD Modul
  RTC_DS1302_module: Arduino module DS1302 SPI Real Time Clock
